// Logisim project Atv1.circ as structural Verilog: 5 circuits, main circuit Ex1
module Ex1 (
  input  A,
  input  B,
  input  C,
  output out_4
);

  wire not_1_out, or_1_out, or_2_out;

  not not_1 (not_1_out, B);
  or or_1 (or_1_out, A, B);
  or or_2 (or_2_out, not_1_out, C);
  and and_1 (out_4, or_1_out, or_2_out);

  // Notes on the sheet:
  //   S = (A + B).(~B + C)
endmodule

module Ex2 (
  input  A,
  input  B,
  input  C,
  output out_4
);

  wire and_1_out, and_2_out, and_3_out, not_1_out, not_2_out;

  not not_1 (not_1_out, A);
  and and_1 (and_1_out, A, C);
  and and_2 (and_2_out, B, C);
  and and_3 (and_3_out, not_1_out, B, C);
  not not_2 (not_2_out, and_2_out);
  or or_1 (out_4, and_1_out, not_2_out, and_3_out);

  // Notes on the sheet:
  //   S = A.C + ~(B.C) + ~A.B.C
endmodule

module Ex3 (
  input  A,
  input  B,
  input  C,
  input  D,
  output out_5
);

  wire and_1_out, and_2_out, not_1_out, not_2_out;

  and and_1 (and_1_out, A, B);
  not not_1 (not_1_out, C);
  and and_2 (and_2_out, C, D);
  not not_2 (not_2_out, and_2_out);
  or or_1 (out_5, and_1_out, not_1_out, not_2_out);

  // Notes on the sheet:
  //   S = A.B + ~C + ~(C.D)
endmodule

module Ex4 (
  input  X,
  input  Y,
  input  W,
  output out_4
);

  wire not_1_out, or_1_out;

  not not_1 (not_1_out, Y);
  or or_1 (or_1_out, not_1_out, W);
  and and_1 (out_4, X, or_1_out);

  // Notes on the sheet:
  //   Z = X.(~Y + W)
endmodule

module Ex5 (
  input  A,
  input  B,
  output out_3
);

  wire and_1_out, and_2_out, not_1_out, not_2_out;

  not not_1 (not_1_out, A);
  not not_2 (not_2_out, B);
  and and_1 (and_1_out, not_1_out, B);
  and and_2 (and_2_out, A, not_2_out);
  or or_1 (out_3, and_1_out, and_2_out);

  // Notes on the sheet:
  //   S = (~A.B) + (~B.A)
  //   Esse circuito se compara a porta "Ou-Exclusivo" pois S será verdadeiro se, e somente se, apenas um elemento de entrada for positivo
endmodule
