// Logisim project Memoria.circ as structural Verilog: 1 circuit, main circuit main
module main (
  input  [3:0] \Endereço ,
  input  [7:0] Etrada,
  input  Escrita,
  input  \Seleção_da_Memória ,
  input  Leitura,
  output [7:0] \Saída 
);

  wire Clock_out, Limpar_out;

  Button Clock (.out(Clock_out));
  Button Limpar (.out(Limpar_out));
  RAM #(.addrWidth(4), .bus("separate")) ram_1 (
    .addr(\Endereço ), .din(Etrada), .data(\Saída ), .str(Escrita), .sel(\Seleção_da_Memória ),
    .clk(Clock_out), .ld(Leitura), .clr(Limpar_out));
endmodule
