// Logisim project Atv2.circ as structural Verilog: 11 circuits, main circuit Meio Somador
module Meio_Somador (
  input  A0,
  input  B0,
  output C0,
  output S0
);

  and and_1 (C0, B0, A0);
  xor xor_1 (S0, A0, B0);
endmodule

module Somador_Completo (
  input  C0,
  input  A1,
  input  B1,
  output C1,
  output S1
);

  wire and_1_out, and_2_out, xor_1_out;

  and and_1 (and_1_out, B1, A1);
  xor xor_1 (xor_1_out, A1, B1);
  and and_2 (and_2_out, C0, xor_1_out);
  xor xor_2 (S1, C0, xor_1_out);
  or or_1 (C1, and_1_out, and_2_out);
endmodule

module Somador_de_2_bits (
  input  A0,
  input  B0,
  input  A1,
  input  B1,
  output C1,
  output S1,
  output S0
);

  wire meio_somador_1_c0;

  Meio_Somador meio_somador_1 (.A0(A0), .B0(B0), .C0(meio_somador_1_c0), .S0(S0));
  Somador_Completo somador_completo_1 (.C0(meio_somador_1_c0), .A1(A1), .B1(B1), .C1(C1), .S1(S1));
endmodule

module Somador_de_4_bits (
  input  in_1,
  input  in_2,
  input  in_3,
  input  in_4,
  input  in_5,
  input  in_6,
  input  in_7,
  input  in_8,
  output out_9,
  output out_10,
  output out_11,
  output out_12,
  output out_13
);

  wire adder_1_cout, adder_2_cout, adder_3_cout;

  Adder #(.width(1)) adder_1 (.a(in_4), .b(in_8), .out(out_9), .cout(adder_1_cout));  // open: cin
  Adder #(.width(1)) adder_2 (.a(in_3), .b(in_7), .out(out_10), .cin(adder_1_cout), .cout(adder_2_cout));
  Adder #(.width(1)) adder_3 (.a(in_2), .b(in_6), .out(out_11), .cin(adder_2_cout), .cout(adder_3_cout));
  Adder #(.width(1)) adder_4 (.a(in_1), .b(in_5), .out(out_12), .cin(adder_3_cout), .cout(out_13));
endmodule

module Somador_de_4_bits_2_0 (
  input  [3:0] in_1,
  input  [3:0] in_2,
  output out_3,
  output [3:0] out_4
);

  Adder #(.width(4)) adder_1 (.a(in_1), .b(in_2), .out(out_4), .cout(out_3));  // open: cin
endmodule

module Somador_de_8_bits (
  input  [3:0] in_1,
  input  [3:0] in_2,
  input  [3:0] in_3,
  input  [3:0] in_4,
  output out_5,
  output [3:0] out_6,
  output [3:0] out_7
);

  wire adder_1_cout;

  Adder #(.width(4)) adder_1 (.a(in_1), .b(in_2), .out(out_7), .cout(adder_1_cout));  // open: cin
  Adder #(.width(4)) adder_2 (.a(in_3), .b(in_4), .out(out_6), .cin(adder_1_cout), .cout(out_5));
endmodule

module Subtrator_de_4_bits (
  input  [3:0] in_1,
  input  [3:0] in_2,
  output out_3,
  output [3:0] out_4
);

  Subtractor #(.width(4)) subtractor_1 (.a(in_1), .b(in_2), .out(out_4), .bout(out_3));  // open: bin
endmodule

module Negador_4_bits (
  input  [3:0] in_1,
  output [3:0] out_2
);

  Negator #(.width(4)) negator_1 (.in(in_1), .out(out_2));

  // Notes on the sheet:
  //   O resultado do negador é o mesmo que o do complemento de dois
endmodule

module \Subtrair_dois_binários_de_4_bits  (
  input  [3:0] A,
  input  [3:0] B,
  output [3:0] out_3,
  output [3:0] out_4
);

  Negator #(.width(4)) negator_1 (.in(B), .out(out_4));
  Adder #(.width(4)) adder_1 (.a(A), .b(out_4), .out(out_3));  // open: cin, cout

  // Notes on the sheet:
  //   Dessa forma, estamos subtraindo A com B, sendo que quando o resultado é negativo ele ja vem com complemento de 2
endmodule

module Multiplicador_de_4_bits (
  input  [3:0] in_1,
  input  [3:0] in_2,
  output [3:0] out_3
);

  Multiplier #(.width(4)) multiplier_1 (.a(in_1), .b(in_2), .out(out_3));  // open: cin, cout
endmodule

module Comparador_de_4_bits (
  input  [3:0] in_1,
  input  [3:0] in_2,
  output out_3,
  output out_4,
  output out_5
);

  Comparator #(.width(4)) comparator_1 (.a(in_1), .b(in_2), .gt(out_3), .eq(out_4), .lt(out_5));
endmodule
