// Logisim project Atv3_Parte1_Decodificadores.circ as structural Verilog: 4 circuits, main circuit Decodificador 2 Bits
module Decodificador_2_Bits (
  input  A0,
  input  A1,
  output D0,
  output D1,
  output D2,
  output D3
);

  and and_1 (D0, ~A1, ~A0);  // AND_Gate
  and and_2 (D1, A1, ~A0);  // AND_Gate
  and and_3 (D2, ~A1, A0);  // AND_Gate
  and and_4 (D3, A1, A0);
endmodule

module Decodificador_3_Bits (
  input  A0,
  input  A1,
  input  A2,
  output D0,
  output D1,
  output D2,
  output D3,
  output D4,
  output D5,
  output D6,
  output D7
);

  and and_1 (D0, ~A2, ~A1, ~A0);  // AND_Gate
  and and_2 (D1, A2, ~A1, ~A0);  // AND_Gate
  and and_3 (D2, ~A2, A1, ~A0);  // AND_Gate
  and and_4 (D3, A2, A1, ~A0);  // AND_Gate
  and and_5 (D4, ~A2, ~A1, A0);  // AND_Gate
  and and_6 (D5, A2, ~A1, A0);  // AND_Gate
  and and_7 (D6, ~A2, A1, A0);  // AND_Gate
  and and_8 (D7, A2, A1, A0);
endmodule

module Decodificador_2_Bits_com_Logisim (
  input  [1:0] in_1,
  output D0,
  output D1,
  output D2,
  output D3
);

  Decoder #(.select(2)) decoder_1 (.out0(D0), .out1(D1), .out2(D2), .out3(D3), .sel(in_1));  // open: en
endmodule

module Decodificador_3_Bits_com_Logisim (
  input  [2:0] in_1,
  output D0,
  output D1,
  output D2,
  output D3,
  output D4,
  output D5,
  output D6,
  output D7
);

  Decoder #(.select(3)) decoder_1 (
    .out0(D0), .out1(D1), .out2(D2), .out3(D3), .out4(D4), .out5(D5), .out6(D6), .out7(D7), .sel(in_1));  // open: en
endmodule
