// Logisim project Atv3_Parte2_Memória.circ as structural Verilog: 1 circuit, main circuit Memória
module \Memória  (
  input  [3:0] \Endereço ,
  input  [7:0] Entrada,
  input  Escrita,
  input  \Seleção_da_Memória ,
  input  Leitura,
  output [7:0] \Saída 
);

  wire Clock_out, Limpar_out;

  Button Clock (.out(Clock_out));
  Button Limpar (.out(Limpar_out));
  RAM #(.addrWidth(4), .bus("separate")) ram_1 (
    .addr(\Endereço ), .din(Entrada), .data(\Saída ), .str(Escrita), .sel(\Seleção_da_Memória ),
    .clk(Clock_out), .ld(Leitura), .clr(Limpar_out));

  // Notes on the sheet:
  //   Nome: MATHEUS
  //   A capacidade de armazenamento é de:  2^Largura do Endereço × Largura dos Dados
  //   Logo: (2^4) x 8 = 128 bits
endmodule
