// Logisim project Atv4_Banco.circ as structural Verilog: 5 circuits, main circuit Decodificador
module Decodificador (
  input  B,
  input  C,
  input  D,
  output a,
  output b_2,
  output c_2,
  output d_2,
  output e,
  output f,
  output g
);

  wire and_1_out, and_2_out, and_3_out, and_4_out, and_5_out, and_6_out, and_7_out, and_8_out, and_10_out,
       and_11_out, and_12_out, and_13_out, and_14_out, not_1_out, not_2_out, not_3_out, not_4_out, not_5_out,
       not_6_out, not_7_out, not_8_out, not_9_out, not_10_out, not_11_out, not_12_out, not_13_out;

  and and_1 (and_1_out, B, D);
  not not_1 (not_1_out, B);
  not not_2 (not_2_out, B);
  not not_3 (not_3_out, C);
  not not_4 (not_4_out, D);
  or or_1 (c_2, D, B);
  not not_5 (not_5_out, B);
  not not_6 (not_6_out, D);
  not not_7 (not_7_out, C);
  not not_8 (not_8_out, D);
  not not_9 (not_9_out, C);
  not not_10 (not_10_out, D);
  not not_11 (not_11_out, B);
  not not_12 (not_12_out, C);
  not not_13 (not_13_out, D);
  or or_2 (a, C, and_1_out);
  and and_2 (and_2_out, not_1_out, D);
  and and_3 (and_3_out, not_2_out, C);
  and and_4 (and_4_out, C, D);
  and and_5 (and_5_out, B, not_3_out, not_4_out);
  and and_6 (and_6_out, not_5_out, C);
  and and_7 (and_7_out, C, not_6_out);
  and and_8 (and_8_out, B, not_7_out, D);
  and and_9 (e, C, not_8_out);
  and and_10 (and_10_out, B, not_9_out);
  and and_11 (and_11_out, B, not_10_out);
  and and_12 (and_12_out, not_11_out, C);
  and and_13 (and_13_out, B, not_12_out);
  and and_14 (and_14_out, B, not_13_out);
  or or_3 (b_2, and_2_out, and_3_out, and_4_out, and_5_out);
  or or_4 (d_2, and_6_out, and_7_out, and_8_out);
  or or_5 (f, and_10_out, and_11_out);
  or or_6 (g, and_12_out, and_13_out, and_14_out);
endmodule

module Codificador (
  input  C1,
  input  D2,
  input  D3,
  input  D4,
  input  D5,
  input  D6,
  input  C7,
  output B,
  output C,
  output D
);

  wire and_1_out, and_2_out, and_3_out, and_4_out, and_5_out, and_6_out, and_7_out, and_8_out, and_9_out,
       and_10_out, and_11_out, and_12_out, not_1_out, not_2_out, not_3_out, not_4_out, not_5_out, not_6_out,
       not_7_out, not_8_out, not_9_out, not_10_out, not_11_out, not_12_out, not_13_out, not_14_out,
       not_15_out, not_16_out, not_17_out, not_18_out, not_19_out, not_20_out, not_21_out, not_22_out,
       not_23_out, not_24_out, not_25_out, not_26_out, not_27_out, not_28_out, not_29_out, not_30_out,
       not_31_out, not_32_out, not_33_out, not_34_out, not_35_out, not_36_out, not_37_out, not_38_out,
       not_39_out, not_40_out, not_41_out, not_42_out, not_43_out, not_44_out, not_45_out, not_46_out,
       not_47_out, not_48_out, not_49_out, not_50_out, not_51_out, not_52_out, not_53_out, not_54_out,
       not_55_out, not_56_out, not_57_out, not_58_out, not_59_out, not_60_out, not_61_out, not_62_out,
       not_63_out, not_64_out, not_65_out, not_66_out, not_67_out, not_68_out, not_69_out, not_70_out,
       not_71_out, not_72_out;

  not not_1 (not_1_out, C1);
  not not_2 (not_2_out, D2);
  not not_3 (not_3_out, D3);
  not not_4 (not_4_out, D4);
  not not_5 (not_5_out, D5);
  not not_6 (not_6_out, D6);
  not not_7 (not_7_out, C1);
  not not_8 (not_8_out, D2);
  not not_9 (not_9_out, D3);
  not not_10 (not_10_out, D4);
  not not_11 (not_11_out, D5);
  not not_12 (not_12_out, C7);
  not not_13 (not_13_out, C1);
  not not_14 (not_14_out, D2);
  not not_15 (not_15_out, D3);
  not not_16 (not_16_out, D4);
  not not_17 (not_17_out, D6);
  not not_18 (not_18_out, C7);
  not not_19 (not_19_out, C1);
  not not_20 (not_20_out, D2);
  not not_21 (not_21_out, D3);
  not not_22 (not_22_out, D5);
  not not_23 (not_23_out, D6);
  not not_24 (not_24_out, C7);
  not not_25 (not_25_out, C1);
  not not_26 (not_26_out, D2);
  not not_27 (not_27_out, D3);
  not not_28 (not_28_out, D4);
  not not_29 (not_29_out, D5);
  not not_30 (not_30_out, D6);
  not not_31 (not_31_out, C1);
  not not_32 (not_32_out, D2);
  not not_33 (not_33_out, D3);
  not not_34 (not_34_out, D4);
  not not_35 (not_35_out, D5);
  not not_36 (not_36_out, C7);
  not not_37 (not_37_out, C1);
  not not_38 (not_38_out, D2);
  not not_39 (not_39_out, D4);
  not not_40 (not_40_out, D5);
  not not_41 (not_41_out, D6);
  not not_42 (not_42_out, C7);
  not not_43 (not_43_out, C1);
  not not_44 (not_44_out, D3);
  not not_45 (not_45_out, D4);
  not not_46 (not_46_out, D5);
  not not_47 (not_47_out, D6);
  not not_48 (not_48_out, C7);
  not not_49 (not_49_out, C1);
  not not_50 (not_50_out, D2);
  not not_51 (not_51_out, D3);
  not not_52 (not_52_out, D4);
  not not_53 (not_53_out, D5);
  not not_54 (not_54_out, D6);
  not not_55 (not_55_out, C1);
  not not_56 (not_56_out, D2);
  not not_57 (not_57_out, D3);
  not not_58 (not_58_out, D4);
  not not_59 (not_59_out, D6);
  not not_60 (not_60_out, C7);
  not not_61 (not_61_out, C1);
  not not_62 (not_62_out, D2);
  not not_63 (not_63_out, D4);
  not not_64 (not_64_out, D5);
  not not_65 (not_65_out, D6);
  not not_66 (not_66_out, C7);
  not not_67 (not_67_out, D2);
  not not_68 (not_68_out, D3);
  not not_69 (not_69_out, D4);
  not not_70 (not_70_out, D5);
  not not_71 (not_71_out, D6);
  not not_72 (not_72_out, C7);
  and and_1 (and_1_out, not_1_out, not_2_out, not_3_out, not_4_out, not_5_out, not_6_out, C7);
  and and_2 (and_2_out, not_7_out, not_8_out, not_9_out, not_10_out, not_11_out, D6, not_12_out);
  and and_3 (and_3_out, not_13_out, not_14_out, not_15_out, not_16_out, D5, not_17_out, not_18_out);
  and and_4 (and_4_out, not_19_out, not_20_out, not_21_out, D4, not_22_out, not_23_out, not_24_out);
  and and_5 (and_5_out, not_25_out, not_26_out, not_27_out, not_28_out, not_29_out, not_30_out, C7);
  and and_6 (and_6_out, not_31_out, not_32_out, not_33_out, not_34_out, not_35_out, D6, not_36_out);
  and and_7 (and_7_out, not_37_out, not_38_out, D3, not_39_out, not_40_out, not_41_out, not_42_out);
  and and_8 (and_8_out, not_43_out, D2, not_44_out, not_45_out, not_46_out, not_47_out, not_48_out);
  and and_9 (and_9_out, not_49_out, not_50_out, not_51_out, not_52_out, not_53_out, not_54_out, C7);
  and and_10 (and_10_out, not_55_out, not_56_out, not_57_out, not_58_out, D5, not_59_out, not_60_out);
  and and_11 (and_11_out, not_61_out, not_62_out, D3, not_63_out, not_64_out, not_65_out, not_66_out);
  and and_12 (and_12_out, C1, not_67_out, not_68_out, not_69_out, not_70_out, not_71_out, not_72_out);
  or or_1 (B, and_1_out, and_2_out, and_3_out, and_4_out);
  or or_2 (C, and_5_out, and_6_out, and_7_out, and_8_out);
  or or_3 (D, and_9_out, and_10_out, and_11_out, and_12_out);
endmodule

module Banco_1 (
);

  wire _1_out, _2_out, _3_out, _4_out, _5_out, _6_out, _7_out, codificador_1_b, codificador_1_c,
       codificador_1_d, decodificador_1_a, decodificador_1_b_2, decodificador_1_c_2, decodificador_1_d_2,
       decodificador_1_e, decodificador_1_f, decodificador_1_g;

  Button _1 (.out(_1_out));
  Button _2 (.out(_2_out));
  Button _3 (.out(_3_out));
  Button _4 (.out(_4_out));
  Button _5 (.out(_5_out));
  Button _6 (.out(_6_out));
  Button _7 (.out(_7_out));
  Codificador codificador_1 (
    .C1(_1_out), .D2(_2_out), .D3(_3_out), .D4(_4_out), .D5(_5_out), .D6(_6_out), .C7(_7_out),
    .B(codificador_1_b), .C(codificador_1_c), .D(codificador_1_d));
  Decodificador decodificador_1 (
    .B(codificador_1_b), .C(codificador_1_c), .D(codificador_1_d), .a(decodificador_1_a),
    .b_2(decodificador_1_b_2), .c_2(decodificador_1_c_2), .d_2(decodificador_1_d_2), .e(decodificador_1_e),
    .f(decodificador_1_f), .g(decodificador_1_g));
  _7_Segment_Display u_7_segment_display_1 (
    .g(decodificador_1_g), .f(decodificador_1_f), .a(decodificador_1_a), .b(decodificador_1_b_2),
    .e(decodificador_1_e), .d(decodificador_1_d_2), .c(decodificador_1_c_2));  // open: dp
endmodule

module Memoria (
  input  Clock,
  input  B,
  input  C,
  input  D,
  output B_2,
  output C_2,
  output D_2
);

  D_Flip_Flop #(.trigger("falling")) d_ff_1 (.clk(Clock), .D(B), .Q(B_2));  // open: Qn, preset, en, reset
  D_Flip_Flop #(.trigger("falling")) d_ff_2 (.clk(Clock), .D(C), .Q(C_2));  // open: Qn, preset, en, reset
  D_Flip_Flop #(.trigger("falling")) d_ff_3 (.clk(Clock), .D(D), .Q(D_2));  // open: Qn, preset, en, reset
endmodule

module Banco_2 (
);

  wire _1_out, _2_out, _3_out, _4_out, _5_out, _6_out, _7_out, codificador_1_b, codificador_1_c,
       codificador_1_d, decodificador_1_a, decodificador_1_b_2, decodificador_1_c_2, decodificador_1_d_2,
       decodificador_1_e, decodificador_1_f, decodificador_1_g, memoria_1_b_2, memoria_1_c_2, memoria_1_d_2,
       or_1_out;

  Button _1 (.out(_1_out));
  Button _2 (.out(_2_out));
  Button _3 (.out(_3_out));
  Button _4 (.out(_4_out));
  Button _5 (.out(_5_out));
  Button _6 (.out(_6_out));
  Button _7 (.out(_7_out));
  or or_1 (or_1_out, _1_out, _2_out, _3_out, _4_out, _5_out, _6_out, _7_out);
  Codificador codificador_1 (
    .C1(_1_out), .D2(_2_out), .D3(_3_out), .D4(_4_out), .D5(_5_out), .D6(_6_out), .C7(_7_out),
    .B(codificador_1_b), .C(codificador_1_c), .D(codificador_1_d));
  Memoria memoria_1 (
    .Clock(or_1_out), .B(codificador_1_b), .C(codificador_1_c), .D(codificador_1_d), .B_2(memoria_1_b_2),
    .C_2(memoria_1_c_2), .D_2(memoria_1_d_2));
  Decodificador decodificador_1 (
    .B(memoria_1_b_2), .C(memoria_1_c_2), .D(memoria_1_d_2), .a(decodificador_1_a),
    .b_2(decodificador_1_b_2), .c_2(decodificador_1_c_2), .d_2(decodificador_1_d_2), .e(decodificador_1_e),
    .f(decodificador_1_f), .g(decodificador_1_g));
  _7_Segment_Display u_7_segment_display_1 (
    .g(decodificador_1_g), .f(decodificador_1_f), .a(decodificador_1_a), .b(decodificador_1_b_2),
    .e(decodificador_1_e), .d(decodificador_1_d_2), .c(decodificador_1_c_2));  // open: dp

  // Notes on the sheet:
  //   Aluno: Matheus Laurentino
endmodule
