// Logisim project Atv5_Relogio.circ as structural Verilog: 2 circuits, main circuit Cronometro
module Cronometro (
  input  in_1,
  output [3:0] out_2,
  output [3:0] out_3,
  output out_4,
  output out_5
);

  Hex_Digit_Display hex_digit_display_1 (.value(out_3));  // open: dp
  Counter #(.width(4), .max('h9), .trigger("falling")) counter_1 (
    .Q(out_3), .carry(out_4), .clk(out_5));  // open: load, D, count, clr
  Counter #(.width(4), .max('h9), .trigger("falling")) counter_2 (
    .Q(out_2), .carry(out_5), .clk(in_1));  // open: load, D, count, clr
  Hex_Digit_Display hex_digit_display_2 (.value(out_2));  // open: dp
endmodule

module Relogio (
  input  in_1,
  output [3:0] out_2,
  output [3:0] out_3,
  output [3:0] out_4,
  output [3:0] out_5,
  output out_6,
  output out_7,
  output out_8,
  output out_9
);

  Counter #(.width(4), .max('h5), .trigger("falling")) counter_1 (
    .Q(out_2), .carry(out_6), .clk(out_7));  // open: load, D, count, clr
  Counter #(.width(4), .max('h9), .trigger("falling")) counter_2 (
    .Q(out_3), .carry(out_7), .clk(out_8));  // open: load, D, count, clr
  Hex_Digit_Display hex_digit_display_1 (.value(out_3));  // open: dp
  Hex_Digit_Display hex_digit_display_2 (.value(out_2));  // open: dp
  Counter #(.width(4), .max('h5), .trigger("falling")) counter_3 (
    .Q(out_4), .carry(out_8), .clk(out_9));  // open: load, D, count, clr
  Counter #(.width(4), .max('h9), .trigger("falling")) counter_4 (
    .Q(out_5), .carry(out_9), .clk(in_1));  // open: load, D, count, clr
  Hex_Digit_Display hex_digit_display_3 (.value(out_5));  // open: dp
  Hex_Digit_Display hex_digit_display_4 (.value(out_4));  // open: dp
endmodule
